# Fritzing sketch sketch pcb (saved by Fritzing 0.9.3b)
circuit board: 6cm x 2.5cm
breadboards: 1

parts:
  mode = Pushbutton [package="[THT]"]
  Brg- = Pushbutton [package="[THT]"]
  Brg+ = Pushbutton [package="[THT]"]
  J1 = male pin header, 6 pins [form="♂ (male)"]
  J2 = female pin header, 3 pins [form="♀ (female)"]
  R2 = Resistor [tolerance=±5% resistance=470 package=THT]
  R1 = Resistor [tolerance=±5% resistance=100k package=THT]

nets:
  N1: mode.Pin_1, mode.Pin_2, Brg-.Pin_1, Brg-.Pin_2, Brg+.Pin_1, Brg+.Pin_2, R1.Pin_1
  N2: mode.Pin_3, mode.Pin_4, Brg-.Pin_3, Brg-.Pin_4, Brg+.Pin_3, Brg+.Pin_4, J1.pin2, J1.pin3, J1.pin4, J1.pin6, J2.pin1
  N3: J1.pin1, R2.Pin_0
  N4: J1.pin5, J2.pin2, R1.Pin_0
  N5: J2.pin3, R2.Pin_1

notes:
  To battery + 1000uF/6.3
